// Logisim project fibonacci-2.circ as structural Verilog: 2 circuits, main circuit main
module main (
  input  [31:0] n,
  output [31:0] nth
);

  wire clock_1_out, comparator_2_eq, first, register_1_q, slt;
  wire [31:0] a11, a12, a21, a22, aa11, aa12, aa21, aa22, b11, b12, b21, b22, c11, c12, c21, c22, cnt,
       multiplexer_1_out, multiplexer_2_out, multiplexer_3_out, multiplexer_4_out, multiplexer_6_out,
       multiplexer_7_out, multiplexer_8_out, multiplexer_9_out, multiplexer_10_out, multiplexer_11_out, n_t,
       register_2_q, register_4_q, shifter_1_out;
  wire [31:1] and_1_out;

  Comparator #(.width(32)) comparator_1 (.a(cnt), .b(32'h1), .eq(first));  // open: gt, lt
  Multiplexer #(.width(32), .enable("false")) multiplexer_1 (.in0(a11), .in1(c11), .out(multiplexer_1_out), .sel(slt));
  Multiplexer #(.width(32), .enable("false")) multiplexer_2 (.in0(a21), .in1(c21), .out(multiplexer_2_out), .sel(slt));
  Multiplexer #(.width(32), .enable("false")) multiplexer_3 (
    .in0(aa11), .in1(32'h1), .out(multiplexer_3_out), .sel(first));
  Multiplexer #(.width(32), .enable("false")) multiplexer_4 (
    .in0(aa21), .in1(32'h1), .out(multiplexer_4_out), .sel(first));
  Comparator #(.width(32)) comparator_2 (.a(n_t), .b({32{1'b0}}), .eq(comparator_2_eq));  // open: gt, lt
  Multiplexer #(.width(32), .enable("false")) multiplexer_5 (.in0(shifter_1_out), .in1(n), .out(n_t), .sel(first));
  Multiplexer #(.width(32), .enable("false")) multiplexer_6 (
    .in0(multiplexer_1_out), .in1(32'h1), .out(multiplexer_6_out), .sel(first));
  Register #(.width(32)) ans21 (.D(multiplexer_2_out), .Q(a21), .clk(clock_1_out));  // open: en, clr
  Clock clock_1 (.out(clock_1_out));
  Register #(.width(32)) u_a11 (.D(multiplexer_3_out), .Q(b11), .clk(clock_1_out));  // open: en, clr
  Register #(.width(32)) u_a21 (.D(multiplexer_4_out), .Q(b21), .clk(clock_1_out));  // open: en, clr
  Register #(.width(1)) register_1 (.D(comparator_2_eq), .Q(register_1_q), .clk(clock_1_out));  // open: en, clr
  Register #(.width(32)) register_2 (.D(n_t), .Q(register_2_q), .clk(clock_1_out));  // open: en, clr
  Register #(.width(32)) ans11 (.D(multiplexer_6_out), .Q(a11), .clk(clock_1_out));  // open: en, clr
  Register #(.width(32)) register_3 (.D(a12), .en(register_1_q), .Q(nth), .clk(clock_1_out));  // open: clr
  assign {and_1_out, slt} = register_2_q & 32'h1;  // AND_Gate and_1, 32 bits wide
  Multiplexer #(.width(32), .enable("false")) multiplexer_7 (.in0(a12), .in1(c12), .out(multiplexer_7_out), .sel(slt));
  Multiplexer #(.width(32), .enable("false")) multiplexer_8 (.in0(a22), .in1(c22), .out(multiplexer_8_out), .sel(slt));
  Multiplexer #(.width(32), .enable("false")) multiplexer_9 (
    .in0(aa12), .in1(32'h1), .out(multiplexer_9_out), .sel(first));
  Multiplexer #(.width(32), .enable("false")) multiplexer_10 (
    .in0(aa22), .in1({32{1'b0}}), .out(multiplexer_10_out), .sel(first));
  Register #(.width(32)) ans12 (.D(multiplexer_7_out), .Q(a12), .clk(clock_1_out));  // open: en, clr
  Multiplexer #(.width(32), .enable("false")) multiplexer_11 (
    .in0(multiplexer_8_out), .in1(32'h1), .out(multiplexer_11_out), .sel(first));
  Register #(.width(32)) u_a12 (.D(multiplexer_9_out), .Q(b12), .clk(clock_1_out));  // open: en, clr
  Register #(.width(32)) u_a22 (.D(multiplexer_10_out), .Q(b22), .clk(clock_1_out));  // open: en, clr
  Shifter #(.width(32), .shift("lr")) shifter_1 (.in(register_2_q), .\dist (5'b00001), .out(shifter_1_out));
  Register #(.width(32)) ans22 (.D(multiplexer_11_out), .Q(a22), .clk(clock_1_out));  // open: en, clr
  matrix_multi matrix_multi_1 (
    .a12(a12), .a22(a22), .b12(b12), .b22(b22), .a11(a11), .a21(a21), .C11(c11), .b11(b11), .C12(c12),
    .b21(b21), .C21(c21), .C22(c22));
  matrix_multi matrix_multi_2 (
    .a12(b12), .a22(b22), .b12(b12), .b22(b22), .a11(b11), .a21(b21), .C11(aa11), .b11(b11), .C12(aa12),
    .b21(b21), .C21(aa21), .C22(aa22));
  Register #(.width(32)) register_4 (.D(cnt), .Q(register_4_q), .clk(clock_1_out));  // open: en, clr
  Adder #(.width(32)) adder_1 (.a(32'h1), .b(register_4_q), .out(cnt));  // open: cin, cout
endmodule

module matrix_multi (
  input  [31:0] a11,
  input  [31:0] a12,
  input  [31:0] a21,
  input  [31:0] a22,
  input  [31:0] b11,
  input  [31:0] b12,
  input  [31:0] b21,
  input  [31:0] b22,
  output [31:0] C11,
  output [31:0] C12,
  output [31:0] C21,
  output [31:0] C22
);

  wire [31:0] multiplier_1_out, multiplier_2_out, multiplier_3_out, multiplier_4_out, multiplier_5_out,
       multiplier_6_out, multiplier_7_out, multiplier_8_out;

  Multiplier #(.width(32)) multiplier_1 (.a(a11), .b(b11), .out(multiplier_1_out));  // open: cin, cout
  Multiplier #(.width(32)) multiplier_2 (.a(a12), .b(b21), .out(multiplier_2_out));  // open: cin, cout
  Multiplier #(.width(32)) multiplier_3 (.a(a11), .b(b12), .out(multiplier_3_out));  // open: cin, cout
  Multiplier #(.width(32)) multiplier_4 (.a(a12), .b(b22), .out(multiplier_4_out));  // open: cin, cout
  Multiplier #(.width(32)) multiplier_5 (.a(a21), .b(b11), .out(multiplier_5_out));  // open: cin, cout
  Multiplier #(.width(32)) multiplier_6 (.a(a22), .b(b21), .out(multiplier_6_out));  // open: cin, cout
  Multiplier #(.width(32)) multiplier_7 (.a(a21), .b(b21), .out(multiplier_7_out));  // open: cin, cout
  Multiplier #(.width(32)) multiplier_8 (.a(a22), .b(b22), .out(multiplier_8_out));  // open: cin, cout
  Adder #(.width(32)) adder_1 (.a(multiplier_1_out), .b(multiplier_2_out), .out(C11));  // open: cin, cout
  Adder #(.width(32)) adder_2 (.a(multiplier_3_out), .b(multiplier_4_out), .out(C12));  // open: cin, cout
  Adder #(.width(32)) adder_3 (.a(multiplier_5_out), .b(multiplier_6_out), .out(C21));  // open: cin, cout
  Adder #(.width(32)) adder_4 (.a(multiplier_7_out), .b(multiplier_8_out), .out(C22));  // open: cin, cout
endmodule
