// Logisim project T1.circ as structural Verilog: 2 circuits, main circuit Sokoban
module Sokoban (
  input  dx,
  input  dy,
  input  reset,
  input  clk,
  output out,
  output flag
);

  wire comparator_1_eq, comparator_2_eq, flag_t;
  wire [2:0] fsm_1_xnext, fsm_1_ynext, x, y;

  Register #(.width(3)) register_1 (.D(fsm_1_xnext), .Q(x), .clk(clk), .clr(reset));  // open: en
  Register #(.width(3)) register_2 (.D(fsm_1_ynext), .Q(y), .clk(clk), .clr(reset));  // open: en
  fsm fsm_1 (.dx(dx), .x(x), .y(y), .dy(dy), .xnext(fsm_1_xnext), .ynext(fsm_1_ynext), .fl(flag_t));
  Register #(.width(1)) register_3 (.D(flag_t), .Q(flag), .clk(clk), .clr(reset));  // open: en
  Comparator #(.width(3), .mode("unsigned")) comparator_1 (.a(x), .b(3'b101), .eq(comparator_1_eq));  // open: gt, lt
  Comparator #(.width(3), .mode("unsigned")) comparator_2 (.a(3'b101), .b(y), .eq(comparator_2_eq));  // open: gt, lt
  and and_1 (out, comparator_1_eq, comparator_2_eq);
endmodule

module fsm (
  input  dx,
  input  [2:0] x,
  input  [2:0] y,
  input  dy,
  output [2:0] xnext,
  output [2:0] ynext,
  output fl
);

  wire and_1_out, and_2_out, and_3_out, and_4_out, and_5_out, and_6_out, comparator_1_gt, comparator_2_gt,
       comparator_3_eq, comparator_4_eq, comparator_5_eq, comparator_6_eq, comparator_7_eq, comparator_8_eq,
       comparator_9_eq, comparator_10_eq, comparator_11_eq, comparator_12_eq, comparator_13_eq,
       comparator_14_eq, fl1, fl2;
  wire [2:0] bit_extender_1_out, bit_extender_2_out, x_dx, y_dy;

  assign bit_extender_1_out = {{2{1'b0}}, dx};  // Bit_Extender bit_extender_1
  assign bit_extender_2_out = {{2{1'b0}}, dy};  // Bit_Extender bit_extender_2
  Adder #(.width(3)) adder_1 (.a(bit_extender_1_out), .b(x), .out(x_dx));  // open: cin, cout
  Adder #(.width(3)) adder_2 (.a(y), .b(bit_extender_2_out), .out(y_dy));  // open: cin, cout
  or or_1 (fl, fl1, fl2);
  Comparator #(.width(3), .mode("unsigned")) comparator_1 (.a(x_dx), .b(3'b101), .gt(comparator_1_gt));  // open: eq, lt
  Comparator #(.width(3), .mode("unsigned")) comparator_2 (.a(y_dy), .b(3'b101), .gt(comparator_2_gt));  // open: eq, lt
  or or_2 (fl1, comparator_1_gt, comparator_2_gt);
  Comparator #(.width(3), .mode("unsigned")) comparator_3 (.a(x_dx), .b(3'b001), .eq(comparator_3_eq));  // open: gt, lt
  Comparator #(.width(3), .mode("unsigned")) comparator_4 (.a(y_dy), .b(3'b001), .eq(comparator_4_eq));  // open: gt, lt
  Comparator #(.width(3), .mode("unsigned")) comparator_5 (.a(x_dx), .b(3'b010), .eq(comparator_5_eq));  // open: gt, lt
  Comparator #(.width(3), .mode("unsigned")) comparator_6 (.a(y_dy), .b(3'b001), .eq(comparator_6_eq));  // open: gt, lt
  Comparator #(.width(3), .mode("unsigned")) comparator_7 (.a(x_dx), .b(3'b001), .eq(comparator_7_eq));  // open: gt, lt
  Comparator #(.width(3), .mode("unsigned")) comparator_8 (.a(y_dy), .b(3'b010), .eq(comparator_8_eq));  // open: gt, lt
  Comparator #(.width(3), .mode("unsigned")) comparator_9 (.a(x_dx), .b(3'b100), .eq(comparator_9_eq));  // open: gt, lt
  Comparator #(.width(3), .mode("unsigned")) comparator_10 (
    .a(y_dy), .b(3'b011), .eq(comparator_10_eq));  // open: gt, lt
  Comparator #(.width(3), .mode("unsigned")) comparator_11 (
    .a(x_dx), .b(3'b100), .eq(comparator_11_eq));  // open: gt, lt
  Comparator #(.width(3), .mode("unsigned")) comparator_12 (
    .a(y_dy), .b(3'b100), .eq(comparator_12_eq));  // open: gt, lt
  Comparator #(.width(3), .mode("unsigned")) comparator_13 (
    .a(x_dx), .b(3'b011), .eq(comparator_13_eq));  // open: gt, lt
  Comparator #(.width(3), .mode("unsigned")) comparator_14 (
    .a(y_dy), .b(3'b100), .eq(comparator_14_eq));  // open: gt, lt
  and and_1 (and_1_out, comparator_3_eq, comparator_4_eq);
  and and_2 (and_2_out, comparator_5_eq, comparator_6_eq);
  and and_3 (and_3_out, comparator_7_eq, comparator_8_eq);
  and and_4 (and_4_out, comparator_9_eq, comparator_10_eq);
  and and_5 (and_5_out, comparator_11_eq, comparator_12_eq);
  and and_6 (and_6_out, comparator_13_eq, comparator_14_eq);
  Multiplexer #(.width(3), .enable("false")) multiplexer_1 (.in0(x_dx), .in1(x), .out(xnext), .sel(fl));
  Multiplexer #(.width(3), .enable("false")) multiplexer_2 (.in0(y_dy), .in1(y), .out(ynext), .sel(fl));
  or or_3 (fl2, and_1_out, and_2_out, and_3_out, and_4_out, and_5_out, and_6_out);
endmodule
