// Logisim project crc.circ as structural Verilog: 2 circuits, main circuit CRC
module CRC (
  input  [7:0] A,
  input  [3:0] B,
  output [10:0] C
);

  wire [2:0] n4div4_1_c, n4div4_2_c, n4div4_3_c, n4div4_4_c, n4div4_5_c, n4div4_7_c;
  wire [3:1] n4div4_6_c;

  _4div4 u_4div4_1 (.A(A[7:4]), .B(B), .C(n4div4_1_c));  // open: D
  _4div4 u_4div4_2 (.A({n4div4_1_c, A[3]}), .B(B), .C(n4div4_2_c));  // open: D
  _4div4 u_4div4_3 (.A({n4div4_2_c, A[2]}), .B(B), .C(n4div4_3_c));  // open: D
  _4div4 u_4div4_4 (.A({n4div4_3_c, A[1]}), .B(B), .C(n4div4_4_c));  // open: D
  _4div4 u_4div4_5 (.A({n4div4_4_c, A[0]}), .B(B), .C(n4div4_5_c));  // open: D
  _4div4 u_4div4_6 (.A({n4div4_5_c, 1'b0}), .B(B), .C(n4div4_6_c));  // open: D
  _4div4 u_4div4_7 (.A({n4div4_6_c, 1'b0}), .B(B), .C(n4div4_7_c));  // open: D
  _4div4 u_4div4_8 (.A({n4div4_7_c, 1'b0}), .B(B), .C(C[2:0]));  // open: D

  assign C[10:3] = A;

  // Other names for the same wires on the sheet: a5 = A[0]; a4 = A[1]; a3 = A[2]; a2 = A[3]; a1[3:0] = A[7:4]
endmodule

module _4div4 (
  input  [3:0] A,
  input  [3:0] B,
  output [2:0] C,
  output D
);

  wire [3:0] xor_1_out;
  wire [3:3] multiplexer_1_out;

  assign xor_1_out = A ^ B;  // XOR_Gate xor_1, 4 bits wide
  Multiplexer #(.width(4), .enable("false")) multiplexer_1 (
    .in0(A), .in1(xor_1_out), .out({multiplexer_1_out[3], C}), .sel(A[3]));

  assign D = A[3];

  // Other names for the same wires on the sheet: fl = A[3]
endmodule
