// Logisim project grf.circ as structural Verilog: 1 circuit, main circuit grf
module grf (
  input  [31:0] WD,
  input  WE,
  input  [4:0] A3,
  input  clk,
  input  reset,
  input  [4:0] A1,
  input  [4:0] A2,
  output [31:0] RD1,
  output [31:0] RD2
);

  wire W0, W1, W2, W3, W4, W5, W6, W7, W8, W9, W10, W11, W12, W13, W14, W15, W16, W17, W18, W19, W20, W21,
       W22, W23, W24, W25, W26, W27, W28, W29, W30, W31;
  wire [31:0] Q0, Q1, Q2, Q3, Q4, Q5, Q6, Q7, Q8, Q9, Q10, Q11, Q12, Q13, Q14, Q15, Q16, Q17, Q18, Q19, Q20,
       Q21, Q22, Q23, Q24, Q25, Q26, Q27, Q28, Q29, Q30, Q31;

  Demultiplexer #(.select(5), .enable("false")) demultiplexer_1 (
    .out0(W0), .out1(W1), .out2(W2), .out3(W3), .out4(W4), .out5(W5), .out6(W6), .out7(W7), .out8(W8),
    .out9(W9), .out10(W10), .out11(W11), .out12(W12), .out13(W13), .out14(W14), .out15(W15), .out16(W16),
    .out17(W17), .out18(W18), .out19(W19), .out20(W20), .out21(W21), .out22(W22), .out23(W23), .out24(W24),
    .out25(W25), .out26(W26), .out27(W27), .out28(W28), .out29(W29), .out30(W30), .out31(W31), .in(WE),
    .sel(A3));
  Multiplexer #(.select(5), .width(32), .enable("false")) multiplexer_1 (
    .in0(Q0), .in1(Q1), .in2(Q2), .in3(Q3), .in4(Q4), .in5(Q5), .in6(Q6), .in7(Q7), .in8(Q8), .in9(Q9),
    .in10(Q10), .in11(Q11), .in12(Q12), .in13(Q13), .in14(Q14), .in15(Q15), .in16(Q16), .in17(Q17),
    .in18(Q18), .in19(Q19), .in20(Q20), .in21(Q21), .in22(Q22), .in23(Q23), .in24(Q24), .in25(Q25),
    .in26(Q26), .in27(Q27), .in28(Q28), .in29(Q29), .in30(Q30), .in31(Q31), .out(RD1), .sel(A1));
  Register #(.width(32)) register_1 (.D({32{1'b0}}), .en(W0), .Q(Q0), .clk(clk), .clr(reset));
  Register #(.width(32)) register_2 (.D(WD), .en(W1), .Q(Q1), .clk(clk), .clr(reset));
  Register #(.width(32)) register_3 (.D(WD), .en(W2), .Q(Q2), .clk(clk), .clr(reset));
  Register #(.width(32)) register_4 (.D(WD), .en(W3), .Q(Q3), .clk(clk), .clr(reset));
  Register #(.width(32)) register_5 (.D(WD), .en(W4), .Q(Q4), .clk(clk), .clr(reset));
  Register #(.width(32)) register_6 (.D(WD), .en(W5), .Q(Q5), .clk(clk), .clr(reset));
  Register #(.width(32)) register_7 (.D(WD), .en(W6), .Q(Q6), .clk(clk), .clr(reset));
  Register #(.width(32)) register_8 (.D(WD), .en(W7), .Q(Q7), .clk(clk), .clr(reset));
  Register #(.width(32)) register_9 (.D(WD), .en(W8), .Q(Q8), .clk(clk), .clr(reset));
  Register #(.width(32)) register_10 (.D(WD), .en(W9), .Q(Q9), .clk(clk), .clr(reset));
  Register #(.width(32)) register_11 (.D(WD), .en(W10), .Q(Q10), .clk(clk), .clr(reset));
  Register #(.width(32)) register_12 (.D(WD), .en(W11), .Q(Q11), .clk(clk), .clr(reset));
  Register #(.width(32)) register_13 (.D(WD), .en(W12), .Q(Q12), .clk(clk), .clr(reset));
  Register #(.width(32)) register_14 (.D(WD), .en(W13), .Q(Q13), .clk(clk), .clr(reset));
  Register #(.width(32)) register_15 (.D(WD), .en(W14), .Q(Q14), .clk(clk), .clr(reset));
  Register #(.width(32)) register_16 (.D(WD), .en(W15), .Q(Q15), .clk(clk), .clr(reset));
  Register #(.width(32)) register_17 (.D(WD), .en(W16), .Q(Q16), .clk(clk), .clr(reset));
  Register #(.width(32)) register_18 (.D(WD), .en(W17), .Q(Q17), .clk(clk), .clr(reset));
  Register #(.width(32)) register_19 (.D(WD), .en(W18), .Q(Q18), .clk(clk), .clr(reset));
  Register #(.width(32)) register_20 (.D(WD), .en(W19), .Q(Q19), .clk(clk), .clr(reset));
  Register #(.width(32)) register_21 (.D(WD), .en(W20), .Q(Q20), .clk(clk), .clr(reset));
  Register #(.width(32)) register_22 (.D(WD), .en(W21), .Q(Q21), .clk(clk), .clr(reset));
  Register #(.width(32)) register_23 (.D(WD), .en(W22), .Q(Q22), .clk(clk), .clr(reset));
  Register #(.width(32)) register_24 (.D(WD), .en(W23), .Q(Q23), .clk(clk), .clr(reset));
  Multiplexer #(.select(5), .width(32), .enable("false")) multiplexer_2 (
    .in0(Q0), .in1(Q1), .in2(Q2), .in3(Q3), .in4(Q4), .in5(Q5), .in6(Q6), .in7(Q7), .in8(Q8), .in9(Q9),
    .in10(Q10), .in11(Q11), .in12(Q12), .in13(Q13), .in14(Q14), .in15(Q15), .in16(Q16), .in17(Q17),
    .in18(Q18), .in19(Q19), .in20(Q20), .in21(Q21), .in22(Q22), .in23(Q23), .in24(Q24), .in25(Q25),
    .in26(Q26), .in27(Q27), .in28(Q28), .in29(Q29), .in30(Q30), .in31(Q31), .out(RD2), .sel(A2));
  Register #(.width(32)) register_25 (.D(WD), .en(W24), .Q(Q24), .clk(clk), .clr(reset));
  Register #(.width(32)) register_26 (.D(WD), .en(W25), .Q(Q25), .clk(clk), .clr(reset));
  Register #(.width(32)) register_27 (.D(WD), .en(W26), .Q(Q26), .clk(clk), .clr(reset));
  Register #(.width(32)) register_28 (.D(WD), .en(W27), .Q(Q27), .clk(clk), .clr(reset));
  Register #(.width(32)) register_29 (.D(WD), .en(W28), .Q(Q28), .clk(clk), .clr(reset));
  Register #(.width(32)) register_30 (.D(WD), .en(W29), .Q(Q29), .clk(clk), .clr(reset));
  Register #(.width(32)) register_31 (.D(WD), .en(W30), .Q(Q30), .clk(clk), .clr(reset));
  Register #(.width(32)) register_32 (.D(WD), .en(W31), .Q(Q31), .clk(clk), .clr(reset));
endmodule
