// Logisim project fsm.circ as structural Verilog: 3 circuits, main circuit fsm
module fsm (
  input  [1:0] in,
  input  reset,
  output Z
);

  wire clock_1_out, comparator_1_eq, comparator_2_eq, comparator_3_eq, not_1_out, or_1_out;
  wire [1:0] and_1_out, bit_extender_1_out, s, snext;

  not not_1 (not_1_out, reset);
  assign bit_extender_1_out = {{1{not_1_out}}, not_1_out};  // Bit_Extender bit_extender_1
  Clock clock_1 (.out(clock_1_out));
  assign and_1_out = bit_extender_1_out & snext;  // AND_Gate and_1, 2 bits wide
  Register #(.width(2)) u_s (.D(and_1_out), .Q(s), .clk(clock_1_out));  // open: en, clr
  fsm_fsm fsm_fsm_1 (.s1(s[1]), .s0(s[0]), .in1(in[1]), .in0(in[0]), .s1n(snext[1]), .s0n(snext[0]));
  Comparator #(.width(2), .mode("unsigned")) comparator_1 (.a(s), .b(2'b10), .eq(comparator_1_eq));  // open: gt, lt
  Comparator #(.width(2), .mode("unsigned")) comparator_2 (.a(2'b00), .b(in), .eq(comparator_2_eq));  // open: gt, lt
  Comparator #(.width(2), .mode("unsigned")) comparator_3 (.a(in), .b(2'b10), .eq(comparator_3_eq));  // open: gt, lt
  or or_1 (or_1_out, comparator_2_eq, comparator_3_eq);
  and and_2 (Z, comparator_1_eq, or_1_out);
endmodule

module fsm_fsm (
  input  s1,
  input  s0,
  input  in1,
  input  in0,
  output s1n,
  output s0n
);

  wire and_2_out, and_3_out, not_1_out, not_2_out, not_3_out, not_4_out, not_5_out, not_6_out;

  not not_1 (not_1_out, s1);
  and and_1 (s1n, not_1_out, s0, not_2_out);
  not not_2 (not_2_out, in0);
  not not_3 (not_3_out, s1);
  and and_2 (and_2_out, not_3_out, not_4_out, in0);
  not not_4 (not_4_out, in1);
  not not_5 (not_5_out, s0);
  and and_3 (and_3_out, not_5_out, not_6_out, in0);
  not not_6 (not_6_out, in1);
  or or_1 (s0n, and_2_out, and_3_out);
endmodule

module fsm_test (
  output CLR,
  output [1:0] in,
  output Z,
  output halt
);

  wire clock_1_out;
  wire [23:0] counter_1_q;

  Counter #(.width(24), .max('hffffff)) counter_1 (
    .Q(counter_1_q), .carry(halt), .clk(clock_1_out));  // open: load, D, count, clr
  Clock clock_1 (.out(clock_1_out));
  RAM #(.addrWidth(24), .dataWidth(3)) ram_1 (.addr(counter_1_q), .data({in, CLR}));  // open: sel, clk, ld, clr
  fsm fsm_1 (.in(in), .Z(Z), .reset(CLR));
endmodule
