// Logisim project ftoi.circ as structural Verilog: 1 circuit, main circuit ftoi
module ftoi (
  input  [15:0] float,
  output [31:0] \int 
);

  wire comparator_1_eq, comparator_2_eq;
  wire [1:0] fl, multiplexer_1_out;
  wire [4:0] adder_1_out, E, subtractor_1_out;
  wire [31:0] adder_2_out, bit_extender_1_out, bit_extender_2_out, multiplexer_2_out, not_1_out, num0, num00,
       num1, num11, num_sign, num_zero;

  Comparator #(.width(5)) comparator_1 (.a(float[14:10]), .b({5{1'b0}}), .eq(comparator_1_eq));  // open: gt, lt
  assign bit_extender_1_out = {{21{1'b0}}, {1'b1, float[9:0]}};  // Bit_Extender bit_extender_1
  Subtractor #(.width(5)) subtractor_1 (.a({5{1'b1}}), .b(E), .out(subtractor_1_out));  // open: bin, bout
  Multiplexer #(.width(2), .enable("false")) multiplexer_1 (
    .in0(2'b00), .in1(2'b01), .out(multiplexer_1_out), .sel(comparator_1_eq));
  Shifter #(.width(32)) shifter_1 (.in(bit_extender_1_out), .\dist (E), .out(num0));
  Adder #(.width(5)) adder_1 (.a(subtractor_1_out), .b(5'b00001), .out(adder_1_out));  // open: cin, cout
  Shifter #(.width(32), .shift("lr")) shifter_2 (.in(num0), .\dist (5'b01010), .out(num00));
  Shifter #(.width(32), .shift("lr")) shifter_3 (.in(num1), .\dist (5'b01010), .out(num11));
  Multiplexer #(.width(32), .enable("false")) multiplexer_2 (
    .in0(num_zero), .in1(num_sign), .out(multiplexer_2_out), .sel(float[15]));
  Multiplexer #(.width(2), .enable("false")) multiplexer_3 (
    .in0(multiplexer_1_out), .in1(2'b10), .out(fl), .sel(comparator_2_eq));
  Comparator #(.width(5)) comparator_2 (.a(float[14:10]), .b({5{1'b1}}), .eq(comparator_2_eq));  // open: gt, lt
  assign bit_extender_2_out = {{22{1'b0}}, float[9:0]};  // Bit_Extender bit_extender_2
  Multiplexer #(.width(32), .enable("false")) multiplexer_4 (.in0(num00), .in1(num11), .out(num_zero), .sel(E[4]));
  Subtractor #(.width(5)) subtractor_2 (.a(float[14:10]), .b(5'b01111), .out(E));  // open: bin, bout
  Shifter #(.width(32), .shift("lr")) shifter_4 (.in(bit_extender_2_out), .\dist (adder_1_out), .out(num1));
  Adder #(.width(32)) adder_2 (.a(num_zero), .b({32{1'b0}}), .out(adder_2_out));  // open: cin, cout
  Multiplexer #(.select(2), .width(32), .enable("false")) multiplexer_5 (
    .in0(multiplexer_2_out), .in1(multiplexer_2_out), .in2({32{1'b0}}), .out(\int ), .sel(fl));  // open: in3
  assign not_1_out = ~adder_2_out;  // NOT_Gate not_1, 32 bits wide
  Adder #(.width(32)) adder_3 (.a(32'h1), .b(not_1_out), .out(num_sign));  // open: cin, cout

  // Other names for the same wires on the sheet: neg = E[4]; exp[4:0] = float[14:10]; sign = float[15];
  //   frac[9:0] = float[9:0]; num[9:0] = float[9:0]
endmodule
